# Fritzing sketch Diagrama SensorIR-ServoMotor (saved by Fritzing 0.9.10b)
breadboards: 1

parts:
  Mod1 = KY-022 Infrared Receiver Module [package="Breakout board"]
  Componente1 = Arduino Uno (Rev3) - ICSP
  J1 = Basic Servo
  J2 = Basic Servo

nets:
  GND: Mod1.-, Componente1.GND, J1.gnd, J2.gnd
  VCC: Mod1.Vin, Componente1.5V, J1.vcc, J2.vcc
  N1: Mod1.S, Componente1.D11_PWM/MOSI
  N2: Componente1.D2, J1.pulse
  N3: Componente1.D3_PWM, J2.pulse

custom parts:
  KY-022 Infrared Receiver Module: KY-022 IR receiver module, reacts to 38kHz infrared light.
